# Fritzing sketch iss_air4 (saved by Fritzing 0.9.1b)

parts:
  Part3 = Arduino Yun
  U2 = mystery part, 4 pins [chip_label=MQ-2]
  DHT2 = DHT22 Humidity and Temperature Sensor
  PPD42NS2 = PPD42NS [package=THT]

nets:
  N1: Part3.A0, U2.pin2, U2.pin3
  N2: Part3.D9_PWM, PPD42NS2.OUTPUT(P2), PPD42NS2.GND
  N3: Part3.D10_PWM/SS, PPD42NS2.OUTPUT(P1), PPD42NS2.VCC
  N4: Part3.D11_PWM/MOSI, DHT2.DATA
  N5: Part3.D12/MISO, U2.pin4

custom parts:
  PPD42NS: A dummy, proxy, ersatz, stand-in part for whatever you want. With 5 pins on a 100 mil inline pin header footprint.
