# Fritzing sketch iss_air5 (saved by Fritzing 0.9.1b)

parts:
  Part3 = Arduino Yun
  U2 = mystery part, 4 pins [chip_label=MQ-2]
  DHT2 = DHT22 Humidity and Temperature Sensor
  PPD42NS2 = PPD42NS [package=THT]
  JP1 = Header 6 [package=1x06_smd_straight_alt]  # not connected
  DHT3 = DHT22 Humidity and Temperature Sensor
  PPD42NS3 = PPD42NS [package=THT]
  R1 = Resistor [tolerance=±5% resistance=220 package=THT]  # not connected
  MQ1 = MQ2 [package=THT]
  Part4 = Arduino Yun
  C1 = Electrolytic Capacitor [capacitance=1µF package="100 mil [THT, electrolytic]"]  # not connected
  proto2 = Adafruit_PermaProto_1_4_Board

nets:
  N1: Part3.A0, U2.pin2, U2.pin3
  N2: Part3.D9_PWM, PPD42NS2.OUTPUT(P2), PPD42NS2.GND
  N3: Part3.D10_PWM/SS, PPD42NS2.OUTPUT(P1), PPD42NS2.VCC
  N4: Part3.D11_PWM/MOSI, DHT2.DATA
  N5: Part3.D12/MISO, U2.pin4
  N6: DHT3.VDD, proto2.connectorY13
  N7: DHT3.DATA, proto2.connectorJ6
  N8: DHT3.GND, proto2.connectorZ13
  N9: PPD42NS3.OUTPUT(P1), proto2.connectorJ7
  N10: PPD42NS3.VCC, proto2.connectorY15
  N11: PPD42NS3.OUTPUT(P2), proto2.connectorJ8
  N12: PPD42NS3.GND, proto2.connectorZ15
  N13: MQ1.VCC, proto2.connectorY11
  N14: MQ1.GND, proto2.connectorZ11
  N15: MQ1.DO, proto2.connectorJ5
  N16: MQ1.AO, Part4.A0
  N17: Part4.VIN, proto2.connectorF2
  N18: proto2.connectorJ2, proto2.connectorY2
  N19: proto2.connectorJ3, proto2.connectorZ3

custom parts:
  PPD42NS: A dummy, proxy, ersatz, stand-in part for whatever you want. With 5 pins on a 100 mil inline pin header footprint.
  MQ2: A dummy, proxy, ersatz, stand-in part for whatever you want. With 4 pins on a 100 mil inline pin header footprint.
